// Logisim project Hangman.circ as structural Verilog: 16 circuits, main circuit main
module main (
  input  [7:0] in_1,
  input  [7:0] in_2,
  input  [7:0] in_3,
  input  [7:0] in_4,
  input  [7:0] in_5,
  input  [7:0] in_6,
  input  [7:0] in_7,
  input  [7:0] in_8,
  input  random_input
);

  wire a_out, and_1_out, and_2_out, b_out, c_out, check_input_1_allowed, check_input_2_allowed,
       check_input_3_allowed, check_input_4_allowed, check_input_5_allowed, check_input_6_allowed,
       check_input_7_allowed, check_input_8_allowed, clock_1_out, d_out, e_out, f_out, g_out, h_out,
       hangman_main_1_finish, hangman_main_1_winner, i_out, j_out, k_out, l_out, letter_board_1_is_pressed,
       m_out, mistakes_parser_1_out_2, mistakes_parser_1_out_3, mistakes_parser_1_out_4,
       mistakes_parser_1_out_5, mistakes_parser_1_out_6, mistakes_parser_1_out_7, mistakes_parser_1_out_8,
       mistakes_parser_1_out_9, mistakes_parser_1_out_10, mistakes_parser_1_out_11, n_out, not_1_out, o_out,
       p_out, q_out, r_out, Reset_out, s_out, Start_out, t_out, u_out, v_out, w_out, x_out, y_out, z_out;
  wire [3:0] counter_1_q, counter_2_q, hangman_main_1_letters_missing, hangman_main_1_mistakes;
  wire [6:0] hangman_main_1_display;
  wire [7:0] check_input_1_out_3, check_input_2_out_3, check_input_3_out_3, check_input_4_out_3,
       check_input_5_out_3, check_input_6_out_3, check_input_7_out_3, check_input_8_out_3,
       letter_board_1_pressed;
  wire [13:0] display_control_1_out_11, display_control_1_out_12, display_control_1_out_13,
       display_control_1_out_14, display_control_1_out_15, display_control_1_out_16,
       display_control_1_out_17, display_control_1_out_18, display_control_1_out_19,
       display_control_1_out_20, display_control_1_out_21, display_control_1_out_22;

  Button a (.out(a_out));
  Button b (.out(b_out));
  Button c (.out(c_out));
  Button d (.out(d_out));
  Button e (.out(e_out));
  Button f (.out(f_out));
  Button g (.out(g_out));
  Button h (.out(h_out));
  Button i (.out(i_out));
  Button j (.out(j_out));
  Button k (.out(k_out));
  Button l (.out(l_out));
  Button m (.out(m_out));
  Button n (.out(n_out));
  Button o (.out(o_out));
  Button p (.out(p_out));
  Button q (.out(q_out));
  Button r (.out(r_out));
  Button s (.out(s_out));
  Button t (.out(t_out));
  Button u (.out(u_out));
  Button v (.out(v_out));
  Button w (.out(w_out));
  Button x (.out(x_out));
  Button y (.out(y_out));
  Button z (.out(z_out));
  Clock clock_1 (.out(clock_1_out));
  Letter_Board letter_board_1 (
    .a(a_out), .b(b_out), .c(c_out), .d(d_out), .e(e_out), .f(f_out), .g(g_out), .h(h_out), .i(i_out),
    .j(j_out), .k(k_out), .l(l_out), .m(m_out), .n(n_out), .o(o_out), .p(p_out), .q(q_out), .r(r_out),
    .s(s_out), .t(t_out), .u(u_out), .v(v_out), .w(w_out), .x(x_out), .y(y_out), .z(z_out),
    .Pressed(letter_board_1_pressed), .Clk(clock_1_out), .is_Pressed(letter_board_1_is_pressed));
  LED led_1 (.in(check_input_1_allowed));
  check_input check_input_1 (.in_1(in_1), .allowed(check_input_1_allowed), .out_3(check_input_1_out_3));
  check_input check_input_2 (.in_1(in_2), .allowed(check_input_2_allowed), .out_3(check_input_2_out_3));
  LED led_2 (.in(check_input_2_allowed));
  check_input check_input_3 (.in_1(in_3), .allowed(check_input_3_allowed), .out_3(check_input_3_out_3));
  LED led_3 (.in(check_input_3_allowed));
  check_input check_input_4 (.in_1(in_4), .allowed(check_input_4_allowed), .out_3(check_input_4_out_3));
  LED led_4 (.in(check_input_4_allowed));
  LED led_5 (.in(check_input_5_allowed));
  check_input check_input_5 (.in_1(in_5), .allowed(check_input_5_allowed), .out_3(check_input_5_out_3));
  check_input check_input_6 (.in_1(in_6), .allowed(check_input_6_allowed), .out_3(check_input_6_out_3));
  LED led_6 (.in(check_input_6_allowed));
  check_input check_input_7 (.in_1(in_7), .allowed(check_input_7_allowed), .out_3(check_input_7_out_3));
  LED led_7 (.in(check_input_7_allowed));
  check_input check_input_8 (.in_1(in_8), .allowed(check_input_8_allowed), .out_3(check_input_8_out_3));
  LED led_8 (.in(check_input_8_allowed));
  Button Reset (.out(Reset_out));
  Button Start (.out(Start_out));
  Hex_Digit_Display hex_digit_display_1 (.value(hangman_main_1_letters_missing));  // open: dp
  Hangman_Main hangman_main_1 (
    .in_1(check_input_1_out_3), .in_2(check_input_2_out_3), .in_3(check_input_3_out_3),
    .in_4(check_input_4_out_3), .in_5(check_input_5_out_3), .in_6(check_input_6_out_3),
    .in_7(check_input_7_out_3), .in_8(check_input_8_out_3), .Reset(Reset_out), .Rand(random_input),
    .Go(Start_out), .guessed_letter(letter_board_1_pressed), .Guessed(letter_board_1_is_pressed),
    .Clk(clock_1_out), .letters_missing(hangman_main_1_letters_missing), .winner(hangman_main_1_winner),
    .finish(hangman_main_1_finish), .mistakes(hangman_main_1_mistakes), .display(hangman_main_1_display));
  TTY tty_1 (.data(hangman_main_1_display), .clk(clock_1_out));  // open: we, clr
  mistakes_parser mistakes_parser_1 (
    .in_1(hangman_main_1_mistakes), .out_2(mistakes_parser_1_out_2), .out_3(mistakes_parser_1_out_3),
    .out_4(mistakes_parser_1_out_4), .out_5(mistakes_parser_1_out_5), .out_6(mistakes_parser_1_out_6),
    .out_7(mistakes_parser_1_out_7), .out_8(mistakes_parser_1_out_8), .out_9(mistakes_parser_1_out_9),
    .out_10(mistakes_parser_1_out_10), .out_11(mistakes_parser_1_out_11));
  DotMatrix #(.matrixcols(12), .matrixrows(14)) dotmatrix_1 (
    .col0(display_control_1_out_21), .col1(display_control_1_out_19), .col2(display_control_1_out_17),
    .col3(display_control_1_out_15), .col4(display_control_1_out_14), .col5(display_control_1_out_13),
    .col6(display_control_1_out_12), .col7(display_control_1_out_11), .col8(display_control_1_out_22),
    .col9(display_control_1_out_20), .col10(display_control_1_out_18), .col11(display_control_1_out_16));
  display_control display_control_1 (
    .in_1(mistakes_parser_1_out_2), .in_2(mistakes_parser_1_out_3), .in_3(mistakes_parser_1_out_4),
    .in_4(mistakes_parser_1_out_5), .in_5(mistakes_parser_1_out_6), .in_6(mistakes_parser_1_out_7),
    .in_7(mistakes_parser_1_out_8), .in_8(mistakes_parser_1_out_9), .in_9(mistakes_parser_1_out_10),
    .in_10(mistakes_parser_1_out_11), .out_21(display_control_1_out_21), .out_19(display_control_1_out_19),
    .out_17(display_control_1_out_17), .out_15(display_control_1_out_15), .out_14(display_control_1_out_14),
    .out_22(display_control_1_out_22), .out_13(display_control_1_out_13), .out_20(display_control_1_out_20),
    .out_12(display_control_1_out_12), .out_18(display_control_1_out_18), .out_11(display_control_1_out_11),
    .out_16(display_control_1_out_16));
  Counter #(.width(4), .max('hf), .ongoal("stay")) counter_1 (
    .count(and_1_out), .Q(counter_1_q), .clk(clock_1_out));  // open: load, D, carry, clr
  not not_1 (not_1_out, hangman_main_1_winner);
  and and_1 (and_1_out, not_1_out, hangman_main_1_finish);
  Hex_Digit_Display hex_digit_display_2 (.value(counter_1_q));  // open: dp
  and and_2 (and_2_out, hangman_main_1_finish, hangman_main_1_winner);
  Hex_Digit_Display hex_digit_display_3 (.value(counter_2_q));  // open: dp
  Counter #(.width(4), .max('hf), .ongoal("stay")) counter_2 (
    .count(and_2_out), .Q(counter_2_q), .clk(clock_1_out));  // open: load, D, carry, clr

  // Notes on the sheet:
  //   Padding should be done on top
  //   unexpected behaviour will occur
  //   counted as multiple mistakes
  //   The indicator will help you to recognise a mistake and light red
  //   If a manual input was taken while one of the lights was red,
  //   Guessing board: Choose the letter you want to guess.
  //   But take care! mutiple tries of the same letter are
  //   Manual Input: Enter the ascii of the letters you want to create a puzzle with
  //   Only supporting lowercase a-z and null for padding the word to 8 letters
  //   Having a null in the middle of the word will also cause unexpected behaviour
  //   To select a manual input, make sure random_input is off before starting
  //   select random_input BEFORE starting
  //   If you want a random letter from the memory
  //   NOTE: For a smooth experience a tick frequency >= 128Hz is recommended
  //   since we are dealing with a display, so some ticks will be used for buffering
  //   Letters to guess
  //   Defeats
  //   Victories
endmodule

module Letter_CU (
  input  Start,
  input  Reset,
  input  Correct,
  input  Is_Zero,
  input  Guess,
  input  Clk,
  output Zero,
  output Take
);

  wire and_1_out, and_3_out, and_4_out, and_5_out, not_1_out, not_2_out, not_3_out, not_4_out, not_5_out,
       not_6_out, not_7_out, not_8_out, not_9_out, or_1_out;
  wire [1:0] or_2_out, register_1_q;

  // Probe on Start
  // Probe on Reset
  // Probe on register_1_q[1]
  // Probe on register_1_q[0]
  // Probe on Correct
  // Probe on Guess
  // Probe on Is_Zero
  or or_1 (or_1_out, register_1_q[1], register_1_q[0]);
  and and_1 (and_1_out, register_1_q[1], register_1_q[0], not_1_out);
  not not_1 (not_1_out, Reset);
  not not_2 (not_2_out, Reset);
  not not_3 (not_3_out, register_1_q[1]);
  not not_4 (not_4_out, register_1_q[0]);
  not not_5 (not_5_out, Reset);
  and and_2 (or_2_out[1], or_1_out, not_6_out);
  not not_6 (not_6_out, Reset);
  and and_3 (and_3_out, register_1_q[1], Guess, Correct, not_2_out);
  and and_4 (and_4_out, not_3_out, not_4_out, Start);
  and and_5 (and_5_out, register_1_q[0], not_5_out, Is_Zero);
  or or_2 (or_2_out[0], and_1_out, and_3_out, and_4_out, and_5_out);
  Register #(.width(2)) register_1 (.D(or_2_out), .Q(register_1_q), .clk(Clk));  // open: en, clr
  // Probe on or_2_out[1]
  // Probe on or_2_out[0]
  not not_7 (not_7_out, register_1_q[0]);
  and and_6 (Zero, not_7_out, not_8_out);
  not not_8 (not_8_out, register_1_q[1]);
  and and_7 (Take, register_1_q[0], not_9_out);
  not not_9 (not_9_out, register_1_q[1]);
endmodule

module Letter_Datapath (
  input  [7:0] Check,
  input  [7:0] Input,
  input  Guess,
  input  Zero,
  input  Take,
  input  Clk,
  output Correct,
  output Is_Zero,
  output Is_Guessed,
  output [7:0] Stored,
  output New_Correct
);

  wire and_1_out, counter_1_q, or_1_out, register_1_q;
  wire [7:0] multiplexer_1_out;

  Multiplexer #(.width(8), .enable("false")) multiplexer_1 (
    .in0(Stored), .in1(Input), .out(multiplexer_1_out), .sel(Take));
  Register Current (.D(multiplexer_1_out), .Q(Stored), .clk(Clk), .clr(counter_1_q));  // open: en
  Counter #(.width(1), .max('h1), .ongoal("stay")) counter_1 (
    .count(Zero), .Q(counter_1_q), .clk(Clk), .clr(counter_1_q));  // open: load, D, carry
  Comparator comparator_1 (.a(Check), .b(Stored), .eq(Correct));  // open: gt, lt
  Comparator comparator_2 (.a({8{1'b0}}), .b(Stored), .eq(Is_Zero));  // open: gt, lt
  and and_1 (and_1_out, Guess, or_1_out);
  or or_1 (or_1_out, Correct, Is_Zero);
  Counter #(.width(1), .max('h1), .ongoal("stay")) counter_2 (
    .count(and_1_out), .Q(Is_Guessed), .clk(Clk), .clr(Take));  // open: load, D, carry
  Register #(.width(1)) register_1 (.D(Is_Guessed), .Q(register_1_q), .clk(Clk), .clr(Take));  // open: en
  xor xor_1 (New_Correct, Is_Guessed, register_1_q);

  // Notes on the sheet:
  //   8-bit Zero
endmodule

module Letter_Main (
  input  [7:0] Checked,
  input  [7:0] Input,
  input  Start,
  input  Reset,
  input  Guess,
  input  Clk,
  output Is_Zero,
  output Is_Guessed,
  output [7:0] Stored,
  output New_Correct
);

  wire letter_cu_1_take, letter_cu_1_zero, letter_datapath_1_correct;

  Letter_CU letter_cu_1 (
    .Start(Start), .Reset(Reset), .Correct(letter_datapath_1_correct), .Is_Zero(Is_Zero), .Guess(Guess),
    .Clk(Clk), .Zero(letter_cu_1_zero), .Take(letter_cu_1_take));
  Letter_Datapath letter_datapath_1 (
    .Check(Checked), .Input(Input), .Guess(Guess), .Zero(letter_cu_1_zero), .Take(letter_cu_1_take),
    .Clk(Clk), .Correct(letter_datapath_1_correct), .Is_Zero(Is_Zero), .Is_Guessed(Is_Guessed),
    .Stored(Stored), .New_Correct(New_Correct));
endmodule

module Hangman_Datapath (
  input  [7:0] Random,
  input  [7:0] in_2,
  input  [7:0] Input,
  input  [7:0] in_4,
  input  [7:0] in_5,
  input  [7:0] in_6,
  input  [7:0] in_7,
  input  [7:0] in_8,
  input  [7:0] in_9,
  input  [7:0] in_10,
  input  [7:0] in_11,
  input  [7:0] in_12,
  input  [7:0] in_13,
  input  [7:0] in_14,
  input  [7:0] in_15,
  input  [7:0] in_16,
  input  [7:0] Guess,
  input  Reset,
  input  Try,
  input  Linput,
  input  LRand,
  input  go,
  input  tick,
  input  update,
  input  Clk,
  output [6:0] to_display,
  output [3:0] Letters_missing,
  output Wrong,
  output Winner,
  output Try_2,
  output Finsih,
  output [3:0] Mistakes
);

  wire and_1_out, and_2_out, and_3_out, c1, c2, c3, c4, c5, c6, c7, c8, comparator_1_eq,
       letter_main_1_is_zero, letter_main_1_new_correct, letter_main_2_is_zero, letter_main_2_new_correct,
       letter_main_3_is_zero, letter_main_3_new_correct, letter_main_4_is_zero, letter_main_4_new_correct,
       letter_main_5_is_zero, letter_main_5_new_correct, letter_main_6_is_zero, letter_main_6_new_correct,
       letter_main_7_is_zero, letter_main_7_new_correct, letter_main_8_is_zero, letter_main_8_new_correct,
       n10delay_1_out_3, n10delay_2_out_3, n10delay_3_out_3, n10hold_1_out_3, not_1_out, not_2_out, or_1_out,
       or_2_out, or_3_out, or_4_out, or_5_out, or_6_out, or_7_out, or_8_out, or_9_out, register_2_q,
       register_3_q;
  wire [3:0] digit_finder_1_out_9;
  wire [7:0] l1, l2, l3, l4, l5, l6, l7, l8, multiplexer_1_out, multiplexer_2_out, multiplexer_3_out,
       multiplexer_4_out, multiplexer_5_out, multiplexer_6_out, multiplexer_7_out, multiplexer_8_out;

  Register #(.width(1)) register_1 (.D(Try), .Q(Try_2), .clk(Clk));  // open: en, clr
  not not_1 (not_1_out, LRand);
  Multiplexer #(.width(8), .enable("false")) multiplexer_1 (
    .in0(Random), .in1(Input), .out(multiplexer_1_out), .sel(not_1_out));
  Multiplexer #(.width(8), .enable("false")) multiplexer_2 (
    .in0(in_2), .in1(in_5), .out(multiplexer_2_out), .sel(not_1_out));
  Letter_Main letter_main_1 (
    .Checked(Guess), .Input(multiplexer_1_out), .Start(go), .Reset(n10delay_3_out_3), .Guess(Try), .Clk(Clk),
    .Is_Guessed(c1), .Stored(l1), .Is_Zero(letter_main_1_is_zero), .New_Correct(letter_main_1_new_correct));
  Multiplexer #(.width(8), .enable("false")) multiplexer_3 (
    .in0(in_4), .in1(in_7), .out(multiplexer_3_out), .sel(not_1_out));
  Multiplexer #(.width(8), .enable("false")) multiplexer_4 (
    .in0(in_6), .in1(in_9), .out(multiplexer_4_out), .sel(not_1_out));
  Letter_Main letter_main_2 (
    .Checked(Guess), .Input(multiplexer_2_out), .Start(go), .Reset(n10delay_3_out_3), .Guess(Try), .Clk(Clk),
    .Is_Guessed(c2), .Stored(l2), .Is_Zero(letter_main_2_is_zero), .New_Correct(letter_main_2_new_correct));
  Multiplexer #(.width(8), .enable("false")) multiplexer_5 (
    .in0(in_8), .in1(in_11), .out(multiplexer_5_out), .sel(not_1_out));
  Letter_Main letter_main_3 (
    .Checked(Guess), .Input(multiplexer_3_out), .Start(go), .Reset(n10delay_3_out_3), .Guess(Try), .Clk(Clk),
    .Is_Guessed(c3), .Stored(l3), .Is_Zero(letter_main_3_is_zero), .New_Correct(letter_main_3_new_correct));
  Multiplexer #(.width(8), .enable("false")) multiplexer_6 (
    .in0(in_10), .in1(in_13), .out(multiplexer_6_out), .sel(not_1_out));
  Multiplexer #(.width(8), .enable("false")) multiplexer_7 (
    .in0(in_12), .in1(in_15), .out(multiplexer_7_out), .sel(not_1_out));
  Letter_Main letter_main_4 (
    .Checked(Guess), .Input(multiplexer_4_out), .Start(go), .Reset(n10delay_3_out_3), .Guess(Try), .Clk(Clk),
    .Is_Guessed(c4), .Stored(l4), .Is_Zero(letter_main_4_is_zero), .New_Correct(letter_main_4_new_correct));
  Counter #(.width(4), .max('ha), .ongoal("stay")) counter_1 (
    .count(tick), .Q(Mistakes), .clk(Clk), .clr(n10delay_3_out_3));  // open: load, D, carry
  Multiplexer #(.width(8), .enable("false")) multiplexer_8 (
    .in0(in_14), .in1(in_16), .out(multiplexer_8_out), .sel(not_1_out));
  Letter_Main letter_main_5 (
    .Checked(Guess), .Input(multiplexer_5_out), .Start(go), .Reset(n10delay_3_out_3), .Guess(Try), .Clk(Clk),
    .Is_Guessed(c5), .Stored(l5), .Is_Zero(letter_main_5_is_zero), .New_Correct(letter_main_5_new_correct));
  _10delay u_10delay_1 (.Start(update), .CLK(Clk), .out_3(n10delay_1_out_3));
  Letter_Main letter_main_6 (
    .Checked(Guess), .Input(multiplexer_6_out), .Start(go), .Reset(n10delay_3_out_3), .Guess(Try), .Clk(Clk),
    .Is_Guessed(c6), .Stored(l6), .Is_Zero(letter_main_6_is_zero), .New_Correct(letter_main_6_new_correct));
  Comparator #(.width(4)) comparator_1 (.a(Mistakes), .b(4'b1010), .eq(comparator_1_eq));  // open: gt, lt
  _10hold u_10hold_1 (.Start(n10delay_1_out_3), .CLK(Clk), .out_3(n10hold_1_out_3));
  Letter_Main letter_main_7 (
    .Checked(Guess), .Input(multiplexer_7_out), .Start(go), .Reset(n10delay_3_out_3), .Guess(Try), .Clk(Clk),
    .Is_Guessed(c7), .Stored(l7), .Is_Zero(letter_main_7_is_zero), .New_Correct(letter_main_7_new_correct));
  or or_1 (or_1_out, c1, n10hold_1_out_3);
  or or_2 (or_2_out, c2, n10hold_1_out_3);
  or or_3 (or_3_out, c3, n10hold_1_out_3);
  or or_4 (or_4_out, c4, n10hold_1_out_3);
  or or_5 (or_5_out, c5, n10hold_1_out_3);
  or or_6 (or_6_out, c6, n10hold_1_out_3);
  or or_7 (or_7_out, c7, n10hold_1_out_3);
  or or_8 (or_8_out, n10hold_1_out_3, c8);
  Letter_Main letter_main_8 (
    .Checked(Guess), .Input(multiplexer_8_out), .Start(go), .Reset(n10delay_3_out_3), .Guess(Try), .Clk(Clk),
    .Is_Guessed(c8), .Stored(l8), .Is_Zero(letter_main_8_is_zero), .New_Correct(letter_main_8_new_correct));
  or or_9 (or_9_out, n10delay_1_out_3, Try_2);
  Digit_Finder digit_finder_1 (
    .in_1(letter_main_1_is_zero), .in_2(letter_main_2_is_zero), .in_3(letter_main_3_is_zero),
    .in_4(letter_main_4_is_zero), .in_5(letter_main_5_is_zero), .in_6(letter_main_6_is_zero),
    .in_7(letter_main_7_is_zero), .in_8(letter_main_8_is_zero), .out_9(digit_finder_1_out_9));
  to_output to_output_1 (
    .in_1(l1), .in_2(l2), .in_3(l3), .in_4(l4), .in_5(l5), .in_6(l6), .in_7(l7), .in_8(l8), .in_9(or_1_out),
    .in_10(or_2_out), .in_11(or_3_out), .in_12(or_4_out), .in_13(or_5_out), .in_14(or_6_out),
    .in_15(or_7_out), .in_16(or_8_out), .Start(or_9_out), .clk(Clk), .to_display(to_display));
  Register #(.width(1)) register_2 (.D(register_3_q), .Q(register_2_q), .clk(Clk));  // open: en, clr
  Register #(.width(1)) register_3 (.D(go), .Q(register_3_q), .clk(Clk));  // open: en, clr
  _10delay u_10delay_2 (.Start(Finsih), .CLK(Clk), .out_3(n10delay_2_out_3));
  _10delay u_10delay_3 (.Start(n10delay_2_out_3), .CLK(Clk), .out_3(n10delay_3_out_3));
  Register #(.width(4)) register_4 (
    .D(digit_finder_1_out_9), .en(register_2_q), .Q(Letters_missing), .clk(Clk), .clr(and_1_out));
  and and_1 (and_1_out, Clk, n10delay_3_out_3);
  nor nor_1 (Wrong, letter_main_8_new_correct, letter_main_7_new_correct, letter_main_6_new_correct, letter_main_5_new_correct, letter_main_4_new_correct, letter_main_3_new_correct, letter_main_2_new_correct, letter_main_1_new_correct);
  not not_2 (not_2_out, Wrong);
  and and_2 (and_2_out, c8, c7, c6, c5, c4, c3, c2, c1);
  and and_3 (and_3_out, not_2_out, and_2_out);
  and and_4 (Winner, update, and_2_out);
  or or_10 (Finsih, and_3_out, Reset, comparator_1_eq);

  // Other names for the same wires on the sheet: r = Reset; t = Try_2; u = update
endmodule

module Hangman_CU (
  input  Go,
  input  Rand,
  input  Finish,
  input  Try,
  input  Wrong,
  input  Clk,
  output Linput,
  output Lrand,
  output count,
  output tick,
  output update
);

  wire and_1_out, and_2_out, and_3_out, and_4_out, and_5_out, and_6_out, and_7_out, and_8_out, and_9_out,
       and_11_out, and_14_out, and_15_out, and_16_out, and_17_out, and_18_out, and_19_out, and_20_out,
       not_1_out, not_2_out, not_3_out, not_4_out, not_5_out, not_6_out, not_7_out, not_8_out, not_9_out,
       not_10_out, not_11_out, not_12_out, not_13_out, not_14_out, not_15_out;
  wire [2:0] or_4_out, register_1_q;

  // Probe on register_1_q[2]
  // Probe on Rand
  // Probe on register_1_q[0]
  // Probe on register_1_q[1]
  // Probe on Go
  not not_1 (not_1_out, register_1_q[2]);
  not not_2 (not_2_out, register_1_q[1]);
  not not_3 (not_3_out, register_1_q[0]);
  not not_4 (not_4_out, Go);
  // Probe on Wrong
  // Probe on Finish
  // Probe on Try
  not not_5 (not_5_out, Rand);
  not not_6 (not_6_out, Finish);
  not not_7 (not_7_out, Try);
  not not_8 (not_8_out, Wrong);
  and and_1 (and_1_out, not_1_out, register_1_q[0], Finish);
  and and_2 (and_2_out, not_1_out, register_1_q[1], Finish);
  and and_3 (and_3_out, not_1_out, register_1_q[1], register_1_q[0], Try, Wrong);
  or or_1 (or_4_out[2], and_1_out, and_2_out, and_3_out);
  and and_4 (and_4_out, not_3_out, not_2_out, register_1_q[2]);
  Register #(.width(3)) register_1 (.D(or_4_out), .Q(register_1_q), .clk(Clk));  // open: en, clr
  and and_5 (and_5_out, not_8_out, Try, not_6_out, not_1_out, register_1_q[0], register_1_q[1]);
  and and_6 (and_6_out, not_6_out, not_7_out, not_1_out, register_1_q[0], register_1_q[1]);
  and and_7 (and_7_out, not_3_out, register_1_q[1], not_1_out, not_6_out);
  and and_8 (and_8_out, not_6_out, register_1_q[0], not_2_out, not_1_out);
  and and_9 (and_9_out, Rand, Go, not_3_out, not_2_out, not_1_out);
  or or_2 (or_4_out[1], and_4_out, and_5_out, and_6_out, and_7_out, and_8_out, and_9_out);
  not not_9 (not_9_out, register_1_q[2]);
  not not_10 (not_10_out, register_1_q[0]);
  not not_11 (not_11_out, register_1_q[2]);
  not not_12 (not_12_out, register_1_q[1]);
  not not_13 (not_13_out, register_1_q[1]);
  and and_10 (Linput, register_1_q[0], not_13_out, not_9_out);
  and and_11 (and_11_out, not_10_out, register_1_q[1], not_11_out);
  or or_3 (count, and_11_out, Linput);
  not not_14 (not_14_out, register_1_q[0]);
  and and_12 (tick, not_14_out, not_12_out, register_1_q[2]);
  not not_15 (not_15_out, register_1_q[1]);
  and and_13 (update, register_1_q[0], not_15_out, register_1_q[2]);
  // Probe on and_11_out
  and and_14 (and_14_out, not_3_out, not_2_out, register_1_q[2]);
  and and_15 (and_15_out, not_8_out, Try, not_6_out, register_1_q[1], register_1_q[0], not_1_out);
  and and_16 (and_16_out, not_7_out, not_6_out, register_1_q[0], register_1_q[1], not_1_out);
  and and_17 (and_17_out, Finish, register_1_q[0], register_1_q[1], not_1_out);
  and and_18 (and_18_out, register_1_q[1], not_3_out, not_1_out);
  and and_19 (and_19_out, register_1_q[0], not_2_out, not_1_out);
  and and_20 (and_20_out, not_5_out, Go, not_3_out, not_2_out, not_1_out);
  // Probe on or_4_out[1]
  // Probe on or_4_out[2]
  // Probe on or_4_out[0]
  or or_4 (or_4_out[0], and_14_out, and_15_out, and_16_out, and_17_out, and_18_out, and_19_out, and_20_out);
endmodule

module Hangman_Main (
  input  [7:0] in_1,
  input  [7:0] in_2,
  input  [7:0] in_3,
  input  [7:0] in_4,
  input  [7:0] in_5,
  input  [7:0] in_6,
  input  [7:0] in_7,
  input  [7:0] in_8,
  input  Reset,
  input  Rand,
  input  Go,
  input  [7:0] guessed_letter,
  input  Guessed,
  input  Clk,
  output [3:0] letters_missing,
  output winner,
  output finish,
  output [3:0] mistakes,
  output [6:0] display
);

  wire hangman_cu_1_linput, hangman_cu_1_tick, hangman_datapath_1_finsih, hangman_datapath_1_try_2,
       hangman_datapath_1_wrong;
  wire [7:0] word_bank_1_letter_1, word_bank_1_letter_2, word_bank_1_letter_3, word_bank_1_letter_4,
       word_bank_1_letter_5, word_bank_1_letter_6, word_bank_1_letter_7, word_bank_1_letter_8;

  Hangman_CU hangman_cu_1 (
    .Go(Go), .Rand(Rand), .Finish(hangman_datapath_1_finsih), .Try(hangman_datapath_1_try_2),
    .Wrong(hangman_datapath_1_wrong), .Clk(Clk), .Linput(hangman_cu_1_linput), .tick(hangman_cu_1_tick),
    .update(finish));  // open: Lrand, count
  Word_Bank word_bank_1 (
    .Clk(Clk), .Letter_1(word_bank_1_letter_1), .Letter_2(word_bank_1_letter_2),
    .Letter_3(word_bank_1_letter_3), .Letter_4(word_bank_1_letter_4), .Letter_5(word_bank_1_letter_5),
    .Letter_6(word_bank_1_letter_6), .Letter_7(word_bank_1_letter_7), .Letter_8(word_bank_1_letter_8));
  Hangman_Datapath hangman_datapath_1 (
    .Random(word_bank_1_letter_1), .in_2(word_bank_1_letter_2), .Input(in_1), .in_4(word_bank_1_letter_3),
    .in_5(in_2), .in_6(word_bank_1_letter_4), .in_7(in_3), .in_8(word_bank_1_letter_5), .in_9(in_4),
    .in_10(word_bank_1_letter_6), .in_11(in_5), .in_12(word_bank_1_letter_7), .in_13(in_6),
    .in_14(word_bank_1_letter_8), .in_15(in_7), .in_16(in_8), .Guess(guessed_letter), .Reset(Reset),
    .Try(Guessed), .Linput(hangman_cu_1_linput), .LRand(Rand), .go(Go), .tick(hangman_cu_1_tick),
    .update(finish), .Clk(Clk), .Letters_missing(letters_missing), .Wrong(hangman_datapath_1_wrong),
    .Winner(winner), .Try_2(hangman_datapath_1_try_2), .Finsih(hangman_datapath_1_finsih),
    .Mistakes(mistakes), .to_display(display));
endmodule

module Word_Bank (
  input  Clk,
  output [7:0] Letter_1,
  output [7:0] Letter_2,
  output [7:0] Letter_3,
  output [7:0] Letter_4,
  output [7:0] Letter_5,
  output [7:0] Letter_6,
  output [7:0] Letter_7,
  output [7:0] Letter_8
);

  wire [1:0] random_2_out;
  wire [4:0] random_1_out;
  wire [31:0] multiplexer_1_out, multiplexer_2_out, multiplexer_3_out, multiplexer_4_out, multiplexer_5_out,
       multiplexer_6_out, multiplexer_7_out, multiplexer_8_out;

  Random #(.width(5)) random_1 (.clk(Clk), .out(random_1_out));  // open: next, clr
  Multiplexer #(.select(5), .width(32), .enable("false")) multiplexer_1 (
    .in0(32'h74696f6e), .in1(32'h79736973), .in2(32'h69636c65), .in3(32'h70656374), .in4(32'h6261636b),
    .in5(32'h61646765), .in6(32'h726f6f6d), .in7(32'h62656566), .in8(32'h6c6f6f64), .in9(32'h6f617264),
    .in10(32'h616e6368), .in11(32'h61626c65), .in12(32'h74746c65), .in13(32'h6c657279), .in14(32'h636b656e),
    .in15(32'h68696c64), .in16(32'h72636c65), .in17(32'h6c617373), .in18(32'h6f766572), .in19(32'h636c7562),
    .in20(32'h6f617374), .in21(32'h636f696c), .in22(32'h6c656765), .in23(32'h74657874), .in24(32'h72616374),
    .in25(32'h72617465), .in26(32'h61796f6e), .in27(32'h63726962), .in28(32'h68696f6e), .in29(32'h62617365),
    .in30(32'h76657279), .in31(32'h6465736b), .out(multiplexer_1_out), .sel(random_1_out));
  Multiplexer #(.select(5), .width(32), .enable("false")) multiplexer_2 (
    .in0(32'h61646469), .in1(32'h616e616c), .in2(32'h617274), .in3(32'h6173), .in4({32{1'b0}}), .in5(32'h62),
    .in6(32'h626564), .in7({32{1'b0}}), .in8(32'h62), .in9(32'h62), .in10(32'h6272), .in11(32'h63),
    .in12(32'h6361), .in13(32'h6365), .in14(32'h636869), .in15(32'h63), .in16(32'h6369), .in17(32'h63),
    .in18(32'h636c), .in19({32{1'b0}}), .in20(32'h63), .in21({32{1'b0}}), .in22(32'h636f6c),
    .in23(32'h636f6e), .in24(32'h636f6e74), .in25(32'h63), .in26(32'h6372), .in27({32{1'b0}}),
    .in28(32'h637573), .in29(32'h64617461), .in30(32'h64656c69), .in31({32{1'b0}}), .out(multiplexer_2_out),
    .sel(random_1_out));
  Multiplexer #(.select(5), .width(32), .enable("false")) multiplexer_3 (
    .in0(32'h7461696c), .in1(32'h73746572), .in2(32'h72696e6b), .in3(32'h666f7274), .in4(32'h72726f72),
    .in5(32'h6d706c65), .in6(32'h66616374), .in7(32'h66656172), .in8(32'h6c696e67), .in9(32'h61766f72),
    .in10(32'h69676874), .in11(32'h6c6f636b), .in12(32'h62616c6c), .in13(32'h72756974), .in14(32'h6675656c),
    .in15(32'h6c617373), .in16(32'h726e6f72), .in17(32'h72617065), .in18(32'h68616972), .in19(32'h68656174),
    .in20(32'h686f6c65), .in21(32'h69646179), .in22(32'h686f7365), .in23(32'h6f74656c), .in24(32'h69636c65),
    .in25(32'h73656374), .in26(32'h6a617a7a), .in27(32'h75696365), .in28(32'h6c616479), .in29(32'h75616765),
    .in30(32'h61756768), .in31(32'h72617279), .out(multiplexer_3_out), .sel(random_1_out));
  Multiplexer #(.select(5), .width(32), .enable("false")) multiplexer_4 (
    .in0(32'h6465), .in1(32'h64697361), .in2(32'h64), .in3(32'h6566), .in4(32'h65), .in5(32'h657861),
    .in6({32{1'b0}}), .in7({32{1'b0}}), .in8(32'h666565), .in9(32'h666c), .in10(32'h666c), .in11(32'h66),
    .in12(32'h666f6f74), .in13(32'h66), .in14({32{1'b0}}), .in15(32'h67), .in16(32'h676f7665), .in17(32'h67),
    .in18({32{1'b0}}), .in19({32{1'b0}}), .in20({32{1'b0}}), .in21(32'h686f6c), .in22({32{1'b0}}),
    .in23(32'h68), .in24(32'h6963), .in25(32'h696e), .in26({32{1'b0}}), .in27(32'h6a), .in28({32{1'b0}}),
    .in29(32'h6c616e67), .in30(32'h6c), .in31(32'h6c6962), .out(multiplexer_4_out), .sel(random_1_out));
  Multiplexer #(.select(5), .width(32), .enable("false")) multiplexer_5 (
    .in0(32'h6c6f7665), .in1(32'h61746368), .in2(32'h65646961), .in3(32'h74696e67), .in4(32'h6d656e75),
    .in5(32'h6d696e64), .in6(32'h7474656e), .in7(32'h6d656e74), .in8(32'h6d6f6f6e), .in9(32'h6f766965),
    .in10(32'h74757265), .in11(32'h626f6f6b), .in12(32'h66696365), .in13(32'h616e6765), .in14(32'h72736f6e),
    .in15(32'h6c616e74), .in16(32'h61796572), .in17(32'h6f696e74), .in18(32'h6c696365), .in19(32'h77646572),
    .in20(32'h6174696f), .in21(32'h626c6963), .in22(32'h75726365), .in23(32'h72696365), .in24(32'h726f6164),
    .in25(32'h6f62696e), .in26(32'h726f6f6d), .in27(32'h7361696c), .in28(32'h686f7265), .in29(32'h73656174),
    .in30(32'h68616b65), .in31(32'h68617065), .out(multiplexer_5_out), .sel(random_1_out));
  Multiplexer #(.select(5), .width(32), .enable("false")) multiplexer_6 (
    .in0({32{1'b0}}), .in1(32'h6d), .in2(32'h6d), .in3(32'h6d6565), .in4({32{1'b0}}), .in5({32{1'b0}}),
    .in6(32'h6d69), .in7(32'h6d6f), .in8({32{1'b0}}), .in9(32'h6d), .in10(32'h6e61), .in11(32'h6e6f7465),
    .in12(32'h6f66), .in13(32'h6f72), .in14(32'h7065), .in15(32'h70), .in16(32'h706c), .in17(32'h70),
    .in18(32'h706f), .in19(32'h706f), .in20(32'h72), .in21(32'h72657075), .in22(32'h7265736f),
    .in23({32{1'b0}}), .in24({32{1'b0}}), .in25(32'h72), .in26({32{1'b0}}), .in27({32{1'b0}}),
    .in28(32'h73656173), .in29({32{1'b0}}), .in30(32'h73), .in31(32'h73), .out(multiplexer_6_out),
    .sel(random_1_out));
  Multiplexer #(.select(5), .width(32), .enable("false")) multiplexer_7 (
    .in0(32'h68656570), .in1(32'h6b697274), .in2(32'h6c6f7065), .in3(32'h6e616b65), .in4(32'h65657a65),
    .in5(32'h69657479), .in6(32'h736f7274), .in7(32'h6f756e64), .in8(32'h7061726b), .in9(32'h74616765),
    .in10(32'h73746570), .in11(32'h69636b73), .in12(32'h72616765), .in13(32'h64656e74), .in14(32'h63657373),
    .in15(32'h7377696d), .in16(32'h77696e67), .in17(32'h61626c65), .in18(32'h61737465), .in19(32'h7465616d),
    .in20(32'h74757265), .in21(32'h75676874), .in22(32'h726f6e65), .in23(32'h7475726e), .in24(32'h74776967),
    .in25(32'h656c6c61), .in26(32'h7665696e), .in27(32'h73696f6e), .in28(32'h6964656f), .in29(32'h79616765),
    .in30(32'h61737465), .in31(32'h70687972), .out(multiplexer_7_out), .sel(random_1_out));
  Multiplexer #(.select(5), .width(32), .enable("false")) multiplexer_8 (
    .in0(32'h73), .in1(32'h73), .in2(32'h73), .in3(32'h73), .in4(32'h736e), .in5(32'h736f63),
    .in6({32{1'b0}}), .in7(32'h73), .in8(32'h73), .in9(32'h73), .in10({32{1'b0}}), .in11(32'h7374),
    .in12(32'h73746f), .in13(32'h737475), .in14(32'h737563), .in15({32{1'b0}}), .in16(32'h73), .in17(32'h74),
    .in18(32'h74), .in19({32{1'b0}}), .in20(32'h746578), .in21(32'h74686f), .in22(32'h7468),
    .in23({32{1'b0}}), .in24({32{1'b0}}), .in25(32'h756d6272), .in26({32{1'b0}}), .in27(32'h766572),
    .in28(32'h76), .in29(32'h766f), .in30(32'h77), .in31(32'h7a65), .out(multiplexer_8_out),
    .sel(random_1_out));
  Random #(.width(2)) random_2 (.clk(Clk), .out(random_2_out));  // open: next, clr
  Multiplexer #(.select(2), .width(32), .enable("false")) multiplexer_9 (
    .in0(multiplexer_1_out), .in1(multiplexer_3_out), .in2(multiplexer_5_out), .in3(multiplexer_7_out),
    .out({Letter_5, Letter_6, Letter_7, Letter_8}), .sel(random_2_out));
  Multiplexer #(.select(2), .width(32), .enable("false")) multiplexer_10 (
    .in0(multiplexer_2_out), .in1(multiplexer_4_out), .in2(multiplexer_6_out), .in3(multiplexer_8_out),
    .out({Letter_1, Letter_2, Letter_3, Letter_4}), .sel(random_2_out));
endmodule

module Digit_Finder (
  input  in_1,
  input  in_2,
  input  in_3,
  input  in_4,
  input  in_5,
  input  in_6,
  input  in_7,
  input  in_8,
  output [3:0] out_9
);

  wire not_1_out, not_2_out, not_3_out, not_4_out, not_5_out, not_6_out, not_7_out, not_8_out;

  not not_1 (not_1_out, in_1);
  not not_2 (not_2_out, in_2);
  not not_3 (not_3_out, in_3);
  not not_4 (not_4_out, in_4);
  not not_5 (not_5_out, in_5);
  not not_6 (not_6_out, in_6);
  not not_7 (not_7_out, in_7);
  not not_8 (not_8_out, in_8);
  Priority_Encoder #(.select(4)) priority_encoder_1 (
    .in0(1'b1), .in1(not_8_out), .in2(not_7_out), .in3(not_6_out), .in4(not_5_out), .in5(not_4_out),
    .in6(not_3_out), .in7(not_2_out), .in8(not_1_out), .in9(1'b0), .in10(1'b0), .in11(1'b0), .in12(1'b0),
    .in13(1'b0), .in14(1'b0), .in15(1'b0), .out(out_9));  // open: gs, en_out, en_in
endmodule

module Letter_Board (
  input  a,
  input  b,
  input  c,
  input  d,
  input  e,
  input  f,
  input  g,
  input  h,
  input  i,
  input  j,
  input  k,
  input  l,
  input  Clk,
  input  m,
  input  n,
  input  o,
  input  p,
  input  q,
  input  r,
  input  s,
  input  t,
  input  u,
  input  v,
  input  w,
  input  x,
  input  y,
  input  z,
  output [7:0] Pressed,
  output is_Pressed
);

  wire comparator_1_eq, not_1_out, not_2_out, register_1_q;
  wire [4:0] priority_encoder_1_out;

  Priority_Encoder #(.select(5)) priority_encoder_1 (
    .in0(1'b1), .in1(a), .in2(b), .in3(c), .in4(d), .in5(e), .in6(f), .in7(g), .in8(h), .in9(i), .in10(j),
    .in11(k), .in12(l), .in13(m), .in14(n), .in15(o), .in16(p), .in17(q), .in18(r), .in19(s), .in20(t),
    .in21(u), .in22(v), .in23(w), .in24(x), .in25(y), .in26(z), .in27(1'b0), .in28(1'b0), .in29(1'b0),
    .in30(1'b0), .in31(1'b0), .out(priority_encoder_1_out));  // open: gs, en_out, en_in
  Multiplexer #(.select(5), .width(8), .enable("false")) multiplexer_1 (
    .in0({8{1'b0}}), .in1(8'h61), .in2(8'h62), .in3(8'h63), .in4(8'h64), .in5(8'h65), .in6(8'h66),
    .in7(8'h67), .in8(8'h68), .in9(8'h69), .in10(8'h6a), .in11(8'h6b), .in12(8'h6c), .in13(8'h6d),
    .in14(8'h6e), .in15(8'h6f), .in16(8'h70), .in17(8'h71), .in18(8'h72), .in19(8'h73), .in20(8'h74),
    .in21(8'h75), .in22(8'h76), .in23(8'h77), .in24(8'h78), .in25(8'h79), .in26(8'h7a), .out(Pressed),
    .sel(priority_encoder_1_out));  // open: in27, in28, in29, in30, in31
  Comparator comparator_1 (.a(Pressed), .b({8{1'b0}}), .eq(comparator_1_eq));  // open: gt, lt
  not not_1 (not_1_out, comparator_1_eq);
  not not_2 (not_2_out, register_1_q);
  Register #(.width(1)) register_1 (.D(not_1_out), .Q(register_1_q), .clk(Clk));  // open: en, clr
  and and_1 (is_Pressed, not_1_out, not_2_out);
endmodule

module to_output (
  input  [7:0] in_1,
  input  [7:0] in_2,
  input  [7:0] in_3,
  input  [7:0] in_4,
  input  [7:0] in_5,
  input  [7:0] in_6,
  input  [7:0] in_7,
  input  [7:0] in_8,
  input  in_9,
  input  in_10,
  input  in_11,
  input  in_12,
  input  in_13,
  input  in_14,
  input  in_15,
  input  in_16,
  input  Start,
  input  clk,
  output [6:0] to_display
);

  wire comparator_1_eq, counter_1_q, multiplexer_2_out;
  wire [3:0] counter_2_q;
  wire [7:0] multiplexer_1_out, multiplexer_3_out;

  Counter #(.width(1), .max('h1), .ongoal("stay")) counter_1 (
    .count(Start), .Q(counter_1_q), .clk(clk), .clr(comparator_1_eq));  // open: load, D, carry
  Counter #(.width(4), .max('ha), .ongoal("stay")) counter_2 (
    .count(counter_1_q), .Q(counter_2_q), .clk(clk), .clr(comparator_1_eq));  // open: load, D, carry
  Multiplexer #(.select(4), .width(8), .enable("false")) multiplexer_1 (
    .in0({8{1'b0}}), .in1(in_1), .in2(in_2), .in3(in_3), .in4(in_4), .in5(in_5), .in6(in_6), .in7(in_7),
    .in8(in_8), .in9(8'ha), .out(multiplexer_1_out), .sel(counter_2_q));  // open: in10, in11, in12, in13, in14, in15
  Multiplexer #(.select(4), .enable("false")) multiplexer_2 (
    .in0(1'b1), .in1(in_9), .in2(in_10), .in3(in_11), .in4(in_12), .in5(in_13), .in6(in_14), .in7(in_15),
    .in8(in_16), .in9(1'b1), .out(multiplexer_2_out), .sel(counter_2_q));  // open: in10, in11, in12, in13, in14, in15
  Comparator #(.width(4)) comparator_1 (.a(counter_2_q), .b(4'b1010), .eq(comparator_1_eq));  // open: gt, lt
  Multiplexer #(.width(8), .enable("false")) multiplexer_3 (
    .in0(8'h5f), .in1(multiplexer_1_out), .out(multiplexer_3_out), .sel(multiplexer_2_out));
  Bit_Extender #(.out_width(7)) bit_extender_1 (.in(multiplexer_3_out), .out(to_display));
endmodule

module _10delay (
  input  Start,
  input  CLK,
  output out_3
);

  wire counter_1_q, counter_3_q;
  wire [3:0] counter_2_q;

  Counter #(.width(1), .max('h1), .ongoal("stay")) counter_1 (
    .count(Start), .Q(counter_1_q), .clk(CLK), .clr(counter_3_q));  // open: load, D, carry
  Counter #(.width(4), .max('ha), .ongoal("stay")) counter_2 (
    .count(counter_1_q), .Q(counter_2_q), .clk(CLK), .clr(counter_3_q));  // open: load, D, carry
  Counter #(.width(1), .max('h1), .ongoal("stay")) counter_3 (
    .count(out_3), .Q(counter_3_q), .clk(CLK), .clr(counter_3_q));  // open: load, D, carry
  Comparator #(.width(4)) comparator_1 (.a(counter_2_q), .b(4'b1010), .eq(out_3));  // open: gt, lt
endmodule

module _10hold (
  input  Start,
  input  CLK,
  output out_3
);

  wire comparator_1_eq, counter_1_q;
  wire [3:0] counter_3_q;

  Counter #(.width(1), .max('h1), .ongoal("stay")) counter_1 (
    .count(Start), .Q(counter_1_q), .clk(CLK), .clr(comparator_1_eq));  // open: load, D, carry
  Counter #(.width(1), .max('h1), .ongoal("stay")) counter_2 (
    .count(counter_1_q), .carry(out_3), .clk(CLK), .clr(comparator_1_eq));  // open: load, D, Q
  Counter #(.width(4), .max('ha), .ongoal("stay")) counter_3 (
    .count(out_3), .Q(counter_3_q), .clk(CLK), .clr(comparator_1_eq));  // open: load, D, carry
  Comparator #(.width(4)) comparator_1 (.a(counter_3_q), .b(4'b1010), .eq(comparator_1_eq));  // open: gt, lt
endmodule

module check_input (
  input  [7:0] in_1,
  output allowed,
  output [7:0] out_3
);

  wire and_1_out, comparator_1_gt, comparator_2_lt, comparator_3_eq;

  Comparator comparator_1 (.a(in_1), .b(8'h60), .gt(comparator_1_gt));  // open: eq, lt
  Comparator comparator_2 (.a(in_1), .b(8'h7b), .lt(comparator_2_lt));  // open: gt, eq
  Comparator comparator_3 (.a(in_1), .b({8{1'b0}}), .eq(comparator_3_eq));  // open: gt, lt
  and and_1 (and_1_out, comparator_1_gt, comparator_2_lt);
  or or_1 (allowed, and_1_out, comparator_3_eq);
  Multiplexer #(.width(8), .enable("false")) multiplexer_1 (.in0({8{1'b0}}), .in1(in_1), .out(out_3), .sel(allowed));
endmodule

module mistakes_parser (
  input  [3:0] in_1,
  output out_2,
  output out_3,
  output out_4,
  output out_5,
  output out_6,
  output out_7,
  output out_8,
  output out_9,
  output out_10,
  output out_11
);

  wire decoder_1_out1, decoder_1_out2, decoder_1_out3, decoder_1_out4, decoder_1_out5, decoder_1_out6,
       decoder_1_out7, decoder_1_out8, decoder_1_out9;

  Decoder #(.select(4), .enable("false")) decoder_1 (
    .out1(decoder_1_out1), .out2(decoder_1_out2), .out3(decoder_1_out3), .out4(decoder_1_out4),
    .out5(decoder_1_out5), .out6(decoder_1_out6), .out7(decoder_1_out7), .out8(decoder_1_out8),
    .out9(decoder_1_out9), .out10(out_11), .sel(in_1));  // open: out0, out11, out12, out13, out14, out15
  or or_1 (out_2, decoder_1_out1, out_3);
  or or_2 (out_3, decoder_1_out2, out_4);
  or or_3 (out_4, decoder_1_out3, out_5);
  or or_4 (out_5, decoder_1_out4, out_6);
  or or_5 (out_6, decoder_1_out5, out_7);
  or or_6 (out_7, decoder_1_out6, out_8);
  or or_7 (out_8, decoder_1_out7, out_9);
  or or_8 (out_9, decoder_1_out8, out_10);
  or or_9 (out_10, decoder_1_out9, out_11);
endmodule

module display_control (
  input  in_1,
  input  in_2,
  input  in_3,
  input  in_4,
  input  in_5,
  input  in_6,
  input  in_7,
  input  in_8,
  input  in_9,
  input  in_10,
  output [13:0] out_11,
  output [13:0] out_12,
  output [13:0] out_13,
  output [13:0] out_14,
  output [13:0] out_15,
  output [13:0] out_16,
  output [13:0] out_17,
  output [13:0] out_18,
  output [13:0] out_19,
  output [13:0] out_20,
  output [13:0] out_21,
  output [13:0] out_22
);


  assign out_11 = {in_3, 2'b00, {3{in_5}}, 2'b00, in_8, 1'b0, in_10, 2'b00, in_1};
  assign out_12 = {in_3, {7{1'b0}}, in_8, 2'b00, in_10, 1'b0, in_1};
  assign out_13 = {in_3, {12{1'b0}}, in_1};
  assign out_14 = {in_3, {12{1'b0}}, in_1};
  assign out_15 = {in_3, {12{1'b0}}, in_1};
  assign out_16 = {{13{1'b0}}, in_1};
  assign out_17 = {{13{in_2}}, in_1};
  assign out_18 = {{8{1'b0}}, in_7, 2'b00, in_9, 1'b0, in_1};
  assign out_19 = {{13{1'b0}}, in_1};
  assign out_20 = {in_3, 2'b00, {3{in_5}}, 2'b00, in_7, 1'b0, in_9, 2'b00, in_1};
  assign out_21 = {{13{1'b0}}, in_1};
  assign out_22 = {in_3, {2{in_4}}, in_5, 1'b0, in_5, {4{in_6}}, 3'b000, in_1};
endmodule
